# Fritzing sketch Pico-breadboard (saved by Fritzing 0.9.6b)
breadboards: 1

parts:
  Mod1 = Raspberry Pi Pico
  U1 = 74HC595 [package="DIP16 [THT]"]
  Mod2 = Raspberry Pi Pico
  LED1 = LED - 3mm [color="Green (565nm)" package="3 mm [THT]"]
  LED2 = LED - 3mm [color="Green (565nm)" current=0.030 package="3 mm [THT]"]
  LED3 = LED - 3mm [color="Yellow (592nm)" current=0.030 package="3 mm [THT]"]
  LED4 = LED - 3mm [color="Yellow (592nm)" current=0.030 package="3 mm [THT]"]
  LED5 = LED - 3mm [color="Green (565nm)" current=0.030 package="3 mm [THT]"]
  LED6 = LED - 3mm [color="Green (565nm)" current=0.030 package="3 mm [THT]"]
  LED7 = LED - 3mm [color="Yellow (592nm)" current=0.030 package="3 mm [THT]"]
  LED8 = LED - 3mm [color="Yellow (592nm)" current=0.030 package="3 mm [THT]"]
  R1 = Resistor [tolerance=±5% resistance=1k package="2512 [SMD]"]
  R2 = Resistor [tolerance=±5% resistance=1k package="2512 [SMD]"]
  R3 = Resistor [tolerance=±5% resistance=1k package="2512 [SMD]"]
  R4 = Resistor [tolerance=±5% resistance=1k package="2512 [SMD]"]
  R5 = Resistor [tolerance=±5% resistance=1k package="2512 [SMD]"]
  R6 = Resistor [tolerance=±5% resistance=1k package="2512 [SMD]"]
  R7 = Resistor [tolerance=±5% resistance=1k package="2512 [SMD]"]
  R8 = Resistor [tolerance=±5% resistance=1k package="2512 [SMD]"]

nets:
  N1: Mod1.pin_1, U1.SH_CP, Mod2.pin_1
  N2: Mod1.pin_2, U1.ST_CP, Mod2.pin_2
  N3: Mod1.pin_3, Mod1.pin_8, Mod1.pin_13, Mod1.pin_18, Mod1.pin_23, Mod1.pin_28, Mod1.pin_33, Mod1.pin_38, U1.GND, U1.OE, Mod2.pin_3, Mod2.pin_8, Mod2.pin_13, Mod2.pin_18, Mod2.pin_23, Mod2.pin_28, Mod2.pin_33, Mod2.pin_38, LED1.cathode, LED2.cathode, LED3.cathode, LED4.cathode, LED5.cathode, LED6.cathode, LED7.cathode, LED8.cathode
  N4: Mod1.pin_4, U1.DS, Mod2.pin_4
  N5: Mod1.pin_5, Mod2.pin_5
  N6: Mod1.pin_6, Mod2.pin_6
  N7: Mod1.pin_7, Mod2.pin_7
  N8: Mod1.pin_9, Mod2.pin_9
  N9: Mod1.pin_10, Mod2.pin_10
  N10: Mod1.pin_11, Mod2.pin_11
  N11: Mod1.pin_12, Mod2.pin_12
  N12: Mod1.pin_14, Mod2.pin_14
  N13: Mod1.pin_15, Mod2.pin_15
  N14: Mod1.pin_16, Mod2.pin_16
  N15: Mod1.pin_17, Mod2.pin_17
  N16: Mod1.pin_19, Mod2.pin_19
  N17: Mod1.pin_20, Mod2.pin_20
  N18: Mod1.pin_21, Mod2.pin_21
  N19: Mod1.pin_22, Mod2.pin_22
  N20: Mod1.pin_24, Mod2.pin_24
  N21: Mod1.pin_25, Mod2.pin_25
  N22: Mod1.pin_26, Mod2.pin_26
  N23: Mod1.pin_27, Mod2.pin_27
  N24: Mod1.pin_29, Mod2.pin_29
  N25: Mod1.pin_30, Mod2.pin_30
  N26: Mod1.pin_31, Mod2.pin_31
  N27: Mod1.pin_32, Mod2.pin_32
  N28: Mod1.pin_34, Mod2.pin_34
  N29: Mod1.pin_35, Mod2.pin_35
  N30: Mod1.pin_36, Mod2.pin_36
  N31: Mod1.pin_37, Mod2.pin_37
  N32: Mod1.pin_39, Mod2.pin_39
  N33: Mod1.pin_40, U1.VCC, Mod2.pin_40
  N34: U1.Q1, R2.Pin_0
  N35: U1.Q2, R3.Pin_0
  N36: U1.Q3, R4.Pin_0
  N37: U1.Q4, R5.Pin_0
  N38: U1.Q5, R6.Pin_0
  N39: U1.Q6, R7.Pin_0
  N40: U1.Q7, R8.Pin_0
  N41: U1.Q0, R1.Pin_0
  N42: LED1.anode, R1.Pin_1
  N43: LED2.anode, R2.Pin_1
  N44: LED3.anode, R3.Pin_1
  N45: LED4.anode, R4.Pin_1
  N46: LED5.anode, R5.Pin_1
  N47: LED6.anode, R6.Pin_1
  N48: LED7.anode, R8.Pin_1
  N49: LED8.anode, R7.Pin_1

custom parts:
  Raspberry Pi Pico: Raspberry Pi Pico. Based around the RP2040 microcontroller the Pico is a low cost microcontroller device bringing Raspberry Pi quality, cost, and easy of use to the microcontroller space. Jan 2021, Split part in to two versions: tht (this one) and SMD. This one will drill holes for a .1 in header in pcb to allow plugging in the module as well as providing pads to solder the module to the top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
